# Fritzing sketch fritzsketch_airfryer (saved by Fritzing 0.9.3b)
circuit board: 5.16309cm x 3.44981cm
breadboards: 1

parts:
  C1 = Ceramic Capacitor [capacitance=22pF package="100 mil [THT, multilayer]"]
  C2 = Ceramic Capacitor [capacitance=22pF package="100 mil [THT, multilayer]"]
  R2 = Resistor [tolerance=±5% resistance=10k package=THT]
  FTDI = male pin header, 6 pins [form="♂ (male)"]
  LCD = female pin header, 4 pins [form="♀ (female)"]
  FAN = LED - 5mm [color="Blue (430nm)" package="5 mm [THT]"]
  HEAT = LED - 5mm [color="Red (633nm)" package="5 mm [THT]"]
  R3 = Resistor [tolerance=±5% resistance=220 package=THT]
  R4 = Resistor [tolerance=±5% resistance=220 package=THT]
  C4 = Electrolytic Capacitor [capacitance=1µF package="100 mil [THT, electrolytic]"]
  C5 = Electrolytic Capacitor [capacitance=1µF package="100 mil [THT, electrolytic]"]
  ROT_ENC = female pin header, 5 pins [form="♀ (female)"]
  R5 = Resistor [tolerance=±5% resistance=100 package=THT]
  R6 = Resistor [tolerance=±5% resistance=47k package=THT]
  FAN|HEAT|G|12Vo = female pin header, 4 pins [form="♀ (female)"]
  12Vi|G|5Vi = female pin header, 3 pins [form="♀ (female)"]
  XTAL1 = Crystal [frequency="16 Mhz" package=THT]
  IC1 = Voltage Regulator [package=to-92]
  D1 = Rectifier Diode [part_number=1N4001 breakdown_voltage=3.6V package="300 mil [THT]"]
  D2 = Rectifier Diode [part_number=1N4001 package="300 mil [THT]"]
  C3 = Ceramic Capacitor [capacitance=100nF package="200 mil [THT, multilayer]"]
  TEMP = male pin header, 2 pins [form="♂ (male)"]
  SPK = Piezo Speaker
  Atmega328PU = atmega328 [package=dip]

nets:
  GND: C1.0, C2.1, FTDI.pin1, LCD.pin1, FAN.anode, HEAT.anode, C4.-, C5.-, ROT_ENC.pin1, R6.Pin_0, FAN|HEAT|G|12Vo.pin3, 12Vi|G|5Vi.pin2, IC1.GND, SPK.pin1, Atmega328PU.GND, Atmega328PU.D5_(PWM), Atmega328PU.D6_(PWM), Atmega328PU.D10_(PWM), Atmega328PU.D11_(PWM), Atmega328PU.D12, Atmega328PU.D13, Atmega328PU.A0, Atmega328PU.A2, Atmega328PU.A3
  N1: C1.1, XTAL1.pin_0, Atmega328PU.XLAT1
  N2: C2.0, XTAL1.pin_1, Atmega328PU.XLAT2
  5V: R2.Pin_0, LCD.pin2, C4.+, ROT_ENC.pin2, IC1.IN, D1.cathode, D2.cathode, Atmega328PU.VCC, Atmega328PU.AVCC
  N3: R2.Pin_1, C3.0, Atmega328PU.RESET
  N4: FTDI.pin3, D2.anode
  N5: FTDI.pin4, Atmega328PU.D0_(RX)
  N6: FTDI.pin5, Atmega328PU.D1_(TX)
  N7: FTDI.pin6, C3.1
  N8: LCD.pin3, Atmega328PU.A4
  N9: LCD.pin4, Atmega328PU.A5
  N10: FAN.cathode, R4.Pin_1
  N11: HEAT.cathode, R3.Pin_1
  N12: R3.Pin_0, FAN|HEAT|G|12Vo.pin2, Atmega328PU.D8
  N13: R4.Pin_0, FAN|HEAT|G|12Vo.pin1, Atmega328PU.D7
  3.3V: C5.+, IC1.OUT, TEMP.pin1, Atmega328PU.AREF
  N14: ROT_ENC.pin3, Atmega328PU.D2
  N15: ROT_ENC.pin4, Atmega328PU.D3_(PWM)
  N16: ROT_ENC.pin5, Atmega328PU.D4
  N17: R5.Pin_0, Atmega328PU.D9_(PWM)
  N18: R5.Pin_1, SPK.pin2
  N19: R6.Pin_1, TEMP.pin2, Atmega328PU.A1
  N20: FAN|HEAT|G|12Vo.pin4, 12Vi|G|5Vi.pin3
  N21: 12Vi|G|5Vi.pin1, D1.anode
